// Logisim project lab1_1.circ as structural Verilog: 1 circuit, main circuit main
module main (
  input  D0,
  input  D1,
  input  D2,
  input  D3,
  input  D4,
  input  D5,
  input  D6,
  input  D7,
  input  D8,
  input  D9,
  input  D10,
  input  D11,
  input  D12,
  input  D13,
  input  D14,
  input  D15,
  input  S3,
  input  S2,
  input  S1,
  input  in_20,
  output Y
);

  wire and_1_out, and_2_out, and_3_out, and_4_out, and_5_out, and_6_out, and_7_out, and_8_out, and_9_out,
       and_10_out, and_11_out, and_12_out, and_13_out, and_14_out, and_15_out, and_16_out, not_1_out,
       not_2_out, not_3_out, not_4_out;

  not not_1 (not_1_out, S3);
  not not_2 (not_2_out, S2);
  not not_3 (not_3_out, S1);
  not not_4 (not_4_out, in_20);
  and and_1 (and_1_out, D0, not_1_out, not_2_out, not_3_out, not_4_out);
  and and_2 (and_2_out, D1, not_1_out, not_2_out, not_3_out, in_20);
  and and_3 (and_3_out, D2, not_1_out, not_2_out, S1, not_4_out);
  and and_4 (and_4_out, D3, not_1_out, not_2_out, S1, in_20);
  and and_5 (and_5_out, D8, S3, not_2_out, not_3_out, not_4_out);
  and and_6 (and_6_out, D9, S3, not_2_out, not_3_out, in_20);
  and and_7 (and_7_out, D10, S3, not_2_out, S1, not_4_out);
  and and_8 (and_8_out, D11, S3, not_2_out, S1, in_20);
  and and_9 (and_9_out, D4, not_1_out, S2, not_3_out, not_4_out);
  and and_10 (and_10_out, D5, not_1_out, S2, not_3_out, in_20);
  and and_11 (and_11_out, D6, not_1_out, S2, S1, not_4_out);
  and and_12 (and_12_out, D7, not_1_out, S2, S1, in_20);
  and and_13 (and_13_out, D12, S3, S2, not_3_out, not_4_out);
  and and_14 (and_14_out, D13, S3, S2, not_3_out, in_20);
  and and_15 (and_15_out, D14, S3, S2, S1, not_4_out);
  and and_16 (and_16_out, D15, S3, S2, S1, in_20);
  or or_1 (Y, and_1_out, and_2_out, and_3_out, and_4_out, and_9_out, and_10_out, and_11_out, and_12_out, and_5_out, and_6_out, and_7_out, and_8_out, and_13_out, and_14_out, and_15_out, and_16_out);

  // Notes on the sheet:
  //   S0
  //   W5
  //   W6
  //   W7
  //   W8
  //   W0
  //   W1
  //   W2
  //   W3
  //   W4
  //   W9
  //   W10
  //   W11
  //   W12
  //   W13
  //   W14
  //   W15
endmodule
