// Logisim project lab3circuit.circ as structural Verilog: 1 circuit, main circuit main
module main (
  input  _1,
  input  _1_2,
  input  _2,
  input  _2_2,
  input  _3,
  input  _3_2,
  input  _4,
  input  _4_2,
  input  _5,
  input  _5_2,
  input  _6,
  input  _6_2,
  input  _7,
  input  _7_2,
  output A_B,
  output A_B_2,
  output A_B_3
);

  wire and_1_out, and_2_out, and_3_out, and_4_out, and_5_out, and_6_out, and_7_out, and_8_out, and_9_out,
       and_10_out, and_11_out, and_12_out, and_13_out, and_14_out, and_15_out, and_16_out, and_17_out,
       and_18_out, and_19_out, and_20_out, and_21_out, and_22_out, and_23_out, and_24_out, and_25_out,
       and_26_out, and_27_out, and_28_out, not_1_out, not_2_out, not_3_out, not_4_out, not_5_out, not_6_out,
       or_1_out, or_2_out, or_3_out, or_4_out, or_5_out, or_6_out, or_7_out, or_8_out, or_9_out, or_10_out,
       or_11_out, or_12_out, or_13_out, or_14_out, or_15_out, or_16_out;

  or or_1 (or_1_out, _1, _3, _5, _7);
  or or_2 (or_2_out, _2, _3, _6, _7);
  or or_3 (or_3_out, _4, _5, _6, _7);
  not not_1 (not_1_out, or_3_out);
  not not_2 (not_2_out, or_2_out);
  not not_3 (not_3_out, or_1_out);
  not not_4 (not_4_out, or_6_out);
  not not_5 (not_5_out, or_5_out);
  or or_4 (or_4_out, _1_2, _3_2, _5_2, _7_2);
  or or_5 (or_5_out, _2_2, _3_2, _6_2, _7_2);
  or or_6 (or_6_out, _4_2, _5_2, _7_2, _6_2);
  not not_6 (not_6_out, or_4_out);
  and and_1 (and_1_out, not_2_out, or_1_out, not_4_out, not_5_out, not_6_out, not_1_out);
  and and_2 (and_2_out, not_5_out, not_4_out);
  and and_3 (and_3_out, or_1_out, not_4_out, or_5_out, not_6_out);
  and and_4 (and_4_out, or_1_out, or_6_out, not_5_out, not_6_out);
  and and_5 (and_5_out, or_1_out, or_6_out, or_5_out, not_6_out);
  and and_6 (and_6_out, not_3_out, not_4_out, not_5_out, or_4_out);
  and and_7 (and_7_out, not_3_out, not_4_out, or_5_out);
  and and_8 (and_8_out, not_3_out, or_6_out, not_5_out, or_4_out);
  and and_9 (and_9_out, or_6_out, or_5_out);
  and and_10 (and_10_out, not_3_out, or_6_out, or_5_out, or_4_out, or_2_out, or_3_out);
  and and_11 (and_11_out, not_3_out, not_4_out, not_5_out, not_6_out);
  and and_12 (and_12_out, or_1_out, not_4_out, not_5_out, or_4_out);
  and and_13 (and_13_out, or_1_out, not_4_out, or_5_out, or_4_out);
  and and_14 (and_14_out, not_3_out, not_4_out, or_5_out, not_6_out);
  and and_15 (and_15_out, not_3_out, or_6_out, not_5_out, not_6_out);
  and and_16 (and_16_out, or_1_out, or_6_out, not_5_out, or_4_out);
  and and_17 (and_17_out, or_1_out, or_6_out, or_5_out, or_4_out);
  and and_18 (and_18_out, not_3_out, or_6_out, or_5_out, not_6_out);
  or or_7 (or_7_out, and_2_out, and_3_out);
  or or_8 (or_8_out, and_4_out, not_4_out);
  or or_9 (or_9_out, and_5_out, not_5_out, not_4_out);
  or or_10 (or_10_out, and_6_out, or_6_out, or_5_out);
  or or_11 (or_11_out, and_7_out, or_6_out);
  or or_12 (or_12_out, and_8_out, and_9_out);
  or or_13 (or_13_out, and_11_out, and_12_out);
  or or_14 (or_14_out, and_13_out, and_14_out);
  or or_15 (or_15_out, and_15_out, and_16_out);
  or or_16 (or_16_out, and_17_out, and_18_out);
  and and_19 (and_19_out, or_7_out, or_2_out, not_1_out);
  and and_20 (and_20_out, or_8_out, or_3_out, not_2_out);
  and and_21 (and_21_out, or_9_out, or_3_out, or_2_out);
  and and_22 (and_22_out, or_13_out, not_2_out, not_1_out);
  and and_23 (and_23_out, or_14_out, or_2_out, not_1_out);
  and and_24 (and_24_out, or_15_out, or_3_out, not_2_out);
  and and_25 (and_25_out, or_16_out, or_3_out, or_2_out);
  and and_26 (and_26_out, or_10_out, not_2_out, not_1_out);
  and and_27 (and_27_out, or_11_out, or_2_out, not_1_out);
  and and_28 (and_28_out, or_12_out, not_2_out, or_3_out);
  or or_17 (A_B, and_1_out, and_19_out, and_20_out, and_21_out);
  or or_18 (A_B_2, and_26_out, and_27_out, and_28_out, and_10_out);
  or or_19 (A_B_3, and_22_out, and_23_out, and_24_out, and_25_out);

  // Notes on the sheet:
  //   A
  //   A2
  //   A1
  //   A0
  //   B2
  //   B1
  //   B0
  //   B
  //   A>B
  //   A<B
  //   A=B
endmodule
