// Logisim project lab5circuit.circ as structural Verilog: 1 circuit, main circuit main
module main (
  input  in_1,
  input  in_2,
  input  in_3,
  input  in_4,
  input  in_5,
  input  in_6,
  input  in_7,
  input  in_8,
  input  in_9,
  input  in_10,
  input  in_11,
  input  in_12,
  input  in_13,
  output out_14,
  output out_15,
  output out_16,
  output out_17,
  output out_18
);

  wire and_1_out, and_2_out, and_3_out, and_4_out, and_5_out, and_6_out, and_7_out, and_8_out, and_9_out,
       and_10_out, and_11_out, and_12_out, and_13_out, and_14_out, and_15_out, and_16_out, and_17_out,
       and_18_out, and_19_out, and_20_out, and_21_out, multiplexer_1_out, multiplexer_2_out,
       multiplexer_3_out, multiplexer_4_out, not_1_out, not_2_out, not_3_out, not_4_out, not_5_out,
       not_9_out, or_1_out, or_2_out, or_3_out, or_4_out, or_5_out, or_6_out, or_7_out, or_8_out, or_9_out,
       or_10_out, or_11_out, or_12_out, or_13_out, or_14_out, or_15_out, or_16_out, or_17_out, xor_1_out,
       xor_2_out, xor_3_out, xor_4_out, xor_5_out, xor_6_out, xor_7_out, xor_8_out, xor_9_out, xor_10_out,
       xor_11_out, xor_12_out, xor_13_out, xor_14_out, xor_15_out, xor_16_out, xor_17_out, xor_18_out;

  not not_1 (not_1_out, in_5);
  not not_2 (not_2_out, in_6);
  not not_3 (not_3_out, in_7);
  not not_4 (not_4_out, in_8);
  xor xor_1 (xor_1_out, in_7, in_7);
  and and_1 (and_1_out, not_2_out, not_3_out, not_4_out);
  Multiplexer multiplexer_1 (.in0(not_1_out), .in1(in_5), .out(multiplexer_1_out), .sel(in_3));
  Multiplexer multiplexer_2 (.in0(in_7), .in1(in_7), .out(multiplexer_2_out), .sel(in_3));
  Multiplexer multiplexer_3 (.in0(xor_1_out), .in1(in_7), .out(multiplexer_3_out), .sel(in_3));
  Multiplexer multiplexer_4 (.in0(and_1_out), .in1(in_8), .out(multiplexer_4_out), .sel(in_3));
  xor xor_2 (xor_2_out, multiplexer_1_out, in_9);
  or or_1 (or_1_out, multiplexer_1_out, in_9);
  and and_2 (and_2_out, multiplexer_1_out, in_9);
  xor xor_3 (xor_3_out, multiplexer_2_out, in_10);
  or or_2 (or_2_out, multiplexer_2_out, in_10);
  and and_3 (and_3_out, multiplexer_2_out, in_10);
  xor xor_4 (xor_4_out, multiplexer_3_out, in_3);
  or or_3 (or_3_out, multiplexer_3_out, in_3);
  and and_4 (and_4_out, multiplexer_3_out, in_3);
  xor xor_5 (xor_5_out, multiplexer_4_out, in_12);
  or or_4 (or_4_out, multiplexer_4_out, in_12);
  and and_5 (and_5_out, multiplexer_4_out, in_12);
  xor xor_6 (xor_6_out, in_2, xor_2_out);
  and and_6 (and_6_out, in_2, or_1_out);
  and and_7 (and_7_out, or_5_out, or_2_out);
  xor xor_7 (xor_7_out, or_5_out, xor_3_out);
  xor xor_8 (xor_8_out, or_6_out, xor_4_out);
  and and_8 (and_8_out, or_6_out, or_3_out);
  xor xor_9 (xor_9_out, or_7_out, xor_5_out);
  and and_9 (and_9_out, or_7_out, or_4_out);
  or or_5 (or_5_out, and_6_out, and_2_out);
  or or_6 (or_6_out, and_7_out, and_3_out);
  or or_7 (or_7_out, and_8_out, and_4_out);
  or or_8 (or_8_out, and_9_out, and_5_out);
  and and_10 (and_10_out, xor_8_out, xor_9_out);
  and and_11 (and_11_out, xor_7_out, xor_9_out);
  or or_9 (or_9_out, and_11_out, and_10_out, or_8_out);
  xor xor_10 (xor_10_out, xor_6_out, in_4);
  or or_10 (or_10_out, xor_6_out, in_4);
  and and_12 (and_12_out, xor_6_out, in_4);
  xor xor_11 (xor_11_out, xor_7_out, or_9_out);
  or or_11 (or_11_out, xor_7_out, or_9_out);
  and and_13 (and_13_out, xor_7_out, or_9_out);
  xor xor_12 (xor_12_out, xor_8_out, or_9_out);
  or or_12 (or_12_out, xor_8_out, or_9_out);
  and and_14 (and_14_out, xor_8_out, or_9_out);
  xor xor_13 (xor_13_out, xor_9_out, in_13);
  or or_13 (or_13_out, xor_9_out, in_13);
  and and_15 (and_15_out, xor_9_out, in_13);
  xor xor_14 (xor_14_out, in_1, xor_10_out);
  and and_16 (and_16_out, in_1, or_10_out);
  xor xor_15 (xor_15_out, or_14_out, xor_11_out);
  and and_17 (and_17_out, or_14_out, or_11_out);
  xor xor_16 (xor_16_out, or_15_out, xor_12_out);
  and and_18 (and_18_out, or_15_out, or_12_out);
  xor xor_17 (xor_17_out, or_16_out, xor_13_out);
  and and_19 (and_19_out, or_16_out, or_13_out);
  or or_14 (or_14_out, and_16_out, and_12_out);
  or or_15 (or_15_out, and_17_out, and_13_out);
  or or_16 (or_16_out, and_18_out, and_14_out);
  or or_17 (or_17_out, and_19_out, and_15_out);
  or or_18 (out_18, or_17_out, or_9_out);
  not not_5 (not_5_out, in_3);
  // NOT_Gate not_6 has open pins: in=xor_14_out, out=open
  // NOT_Gate not_7 has open pins: in=xor_15_out, out=open
  // NOT_Gate not_8 has open pins: in=xor_16_out, out=open
  not not_9 (not_9_out, xor_17_out);
  and and_20 (and_20_out, not_5_out, in_3);
  xor xor_18 (xor_18_out, xor_15_out, xor_16_out);
  buf and_21 (and_21_out, not_9_out);  // AND_Gate
  Multiplexer multiplexer_5 (.in0(xor_14_out), .out(out_14), .sel(and_20_out));  // open: in1
  Multiplexer multiplexer_6 (.in0(xor_15_out), .in1(xor_15_out), .out(out_15), .sel(and_20_out));
  Multiplexer multiplexer_7 (.in0(xor_18_out), .in1(xor_16_out), .out(out_16), .sel(and_20_out));
  Multiplexer multiplexer_8 (.in0(and_21_out), .in1(xor_17_out), .out(out_17), .sel(and_20_out));

  assign in_11 = in_3;
endmodule
